// Logisim project Simple Logisim CPU by Hudson Lois Marcus.circ as structural Verilog: 15 circuits, main circuit main
module main (
);

  wire alu_1_zero, and_1_out, button_1_out, clock_1_out, control_1_alu_branch, control_1_alu_source,
       control_1_clock_stop, control_1_mem_read, control_1_mem_to_register, control_1_mem_write,
       control_1_reg_dest, control_1_reg_write, control_1_write_ra, not_1_out;
  wire [0:0] and_2_out;
  wire [1:0] control_1_aluop1, control_1_branch_2;
  wire [2:0] multiplexer_1_out, multiplexer_2_out, multiplexer_3_out;
  wire [15:0] adder_1_out, adder_2_out, alu_1_output, bit_extender_1_out, multiplexer_4_out,
       multiplexer_5_out, multiplexer_6_out, PC_q, ra_q, ram_1_dout, ram_2_dout, registers_1_readdata1,
       registers_1_readdata2;

  not not_1 (not_1_out, control_1_clock_stop);
  Clock clock_1 (.out(clock_1_out));
  Button button_1 (.out(button_1_out));
  and and_1 (and_1_out, not_1_out, clock_1_out);
  Register #(.trigger("falling"), .width(16)) PC (
    .D(multiplexer_4_out), .en(1'b1), .Q(PC_q), .clk(and_1_out), .clr(button_1_out));
  RAM #(.addrWidth(16), .dataWidth(16), .enables("line"), .trigger("falling"), .\type ("nonvolatile")) ram_1 (
    .addr(PC_q), .clk(and_1_out), .dout(ram_1_dout));  // open: we, din
  Adder #(.width(16)) adder_1 (.a(16'h1), .b(PC_q), .out(adder_1_out));  // open: cin, cout
  Multiplexer #(.enable("false"), .width(3)) multiplexer_1 (
    .in0(ram_1_dout[8:6]), .in1(ram_1_dout[2:0]), .out(multiplexer_1_out), .sel(control_1_reg_dest));
  Multiplexer #(.enable("false"), .width(3)) multiplexer_2 (
    .in0(ram_1_dout[11:9]), .in1(ram_1_dout[8:6]), .out(multiplexer_2_out), .sel(control_1_reg_dest));
  Multiplexer #(.enable("false"), .width(3)) multiplexer_3 (
    .in0(ram_1_dout[8:6]), .in1(ram_1_dout[5:3]), .out(multiplexer_3_out), .sel(control_1_reg_dest));
  Register #(.trigger("falling"), .width(16)) ra (
    .D(adder_1_out), .en(control_1_write_ra), .Q(ra_q), .clk(and_1_out));  // open: clr
  assign bit_extender_1_out = {{10{ram_1_dout[5]}}, ram_1_dout[5:0]};  // Bit_Extender bit_extender_1
  Control control_1 (
    .in_1(ram_1_dout[15:12]), .reg_write(control_1_reg_write), .ALU_source(control_1_alu_source),
    .reg_dest(control_1_reg_dest), .mem_to_register(control_1_mem_to_register), .ALUOp1(control_1_aluop1[0]),
    .ALUOp2(control_1_aluop1[1]), .clock_stop(control_1_clock_stop), .mem_read(control_1_mem_read),
    .mem_write(control_1_mem_write), .write_ra(control_1_write_ra), .ALU_branch(control_1_alu_branch),
    .branch_2(control_1_branch_2));
  Adder #(.width(16)) adder_2 (.a(PC_q), .b(bit_extender_1_out), .out(adder_2_out));  // open: cin, cout
  and and_2 (and_2_out[0], control_1_branch_2[0], alu_1_zero);
  Multiplexer #(.enable("false"), .select(2), .width(16)) multiplexer_4 (
    .in0(adder_1_out), .in1(adder_2_out), .in2(ra_q), .in3(adder_2_out), .out(multiplexer_4_out),
    .sel({control_1_branch_2[1], and_2_out[0]}));
  Registers registers_1 (
    .WriteReg(multiplexer_1_out), .RegWrite(control_1_reg_write), .Clock(and_1_out),
    .WriteData(multiplexer_6_out), .ReadReg1(multiplexer_2_out), .ReadReg2(multiplexer_3_out),
    .ReadData1(registers_1_readdata1), .ReadData2(registers_1_readdata2));  // open: Reset
  Multiplexer #(.enable("false"), .width(16)) multiplexer_5 (
    .in0(registers_1_readdata2), .in1(bit_extender_1_out), .out(multiplexer_5_out), .sel(control_1_alu_source));
  ALU alu_1 (
    .Data2(multiplexer_5_out), .Data1(registers_1_readdata1), .ALUBranch(control_1_alu_branch),
    .ALUop_2(control_1_aluop1), .Zero(alu_1_zero), .\output (alu_1_output));
  RAM #(.addrWidth(16), .dataWidth(16)) ram_2 (
    .addr(alu_1_output), .we(control_1_mem_write), .oe(control_1_mem_read), .clk(and_1_out),
    .din(registers_1_readdata2), .dout(ram_2_dout));
  Multiplexer #(.enable("false"), .width(16)) multiplexer_6 (
    .in0(alu_1_output), .in1(ram_2_dout), .out(multiplexer_6_out), .sel(control_1_mem_to_register));
endmodule

module regWrite (
  input  [3:0] in_1,
  output out_2
);

  wire and_1_out, and_2_out, and_3_out, and_4_out;

  and and_1 (and_1_out, ~in_1[0], ~in_1[1], ~in_1[3]);  // AND_Gate
  and and_2 (and_2_out, ~in_1[1], ~in_1[2], ~in_1[3]);  // AND_Gate
  and and_3 (and_3_out, ~in_1[1], ~in_1[2], in_1[3]);  // AND_Gate
  and and_4 (and_4_out, in_1[1], ~in_1[3]);  // AND_Gate
  or or_1 (out_2, and_1_out, and_2_out, and_3_out, and_4_out);
endmodule

module writeRa (
  input  [3:0] in_1,
  output out_2
);

  and and_1 (out_2, in_1[0], ~in_1[1], in_1[2], in_1[3]);  // AND_Gate
endmodule

module memWrite (
  input  [3:0] in_1,
  output out_2
);

  and and_1 (out_2, in_1[0], ~in_1[1], in_1[2], ~in_1[3]);  // AND_Gate
endmodule

module memToRegister (
  input  [3:0] in_1,
  output out_2
);

  and and_1 (out_2, ~in_1[0], ~in_1[1], in_1[2], ~in_1[3]);  // AND_Gate
endmodule

module clockStop (
  input  [3:0] in_1,
  output out_2
);

  and and_1 (out_2, in_1[0], in_1[1], in_1[2], in_1[3]);
endmodule

module memRead (
  output out_1
);


  assign out_1 = 1'b1;
endmodule

module ALUBranch (
  input  [3:0] in_1,
  output out_2
);

  and and_1 (out_2, in_1[0], in_1[1], ~in_1[2], in_1[3]);  // AND_Gate
endmodule

module branch (
  input  [3:0] in_1,
  output [1:0] out_2
);

  wire and_1_out, and_2_out, and_3_out, and_4_out;

  and and_1 (and_1_out, in_1[0], ~in_1[1], in_1[2], in_1[3]);  // AND_Gate
  and and_2 (and_2_out, ~in_1[0], in_1[1], in_1[2], in_1[3]);  // AND_Gate
  and and_3 (and_3_out, ~in_1[1], in_1[2], in_1[3]);  // AND_Gate
  and and_4 (and_4_out, in_1[1], ~in_1[2], in_1[3]);  // AND_Gate
  or or_1 (out_2[1], and_1_out, and_2_out);
  or or_2 (out_2[0], and_3_out, and_4_out);
endmodule

module ALUOp (
  input  [3:0] in_1,
  output out_2,
  output out_3
);

  wire and_1_out, and_2_out, and_3_out, and_4_out, and_5_out;

  and and_1 (and_1_out, ~in_1[0], ~in_1[1], in_1[2], ~in_1[3]);  // AND_Gate
  and and_2 (and_2_out, in_1[0], ~in_1[1], ~in_1[2], in_1[3]);  // AND_Gate
  and and_3 (and_3_out, in_1[0], ~in_1[3]);  // AND_Gate
  and and_4 (and_4_out, ~in_1[1], ~in_1[2], in_1[3]);  // AND_Gate
  and and_5 (and_5_out, in_1[1], ~in_1[2], ~in_1[3]);  // AND_Gate
  or or_1 (out_2, and_1_out, and_2_out, and_3_out);
  or or_2 (out_3, and_4_out, and_5_out);
endmodule

module regDest (
  input  [3:0] in_1,
  output out_2
);

  wire and_1_out, and_2_out;

  and and_1 (and_1_out, in_1[0], ~in_1[2], ~in_1[3]);  // AND_Gate
  and and_2 (and_2_out, in_1[1], ~in_1[0], ~in_1[3]);  // AND_Gate
  or or_1 (out_2, and_1_out, and_2_out);
endmodule

module ALU (
  input  [15:0] Data2,
  input  [15:0] Data1,
  input  ALUBranch,
  input  [1:0] ALUop_2,
  output Zero,
  output [15:0] \output 
);

  wire ble_out, bne_out, comparator_1_eq, comparator_1_lt;
  wire [15:0] adder_1_out, and_1_out, or_1_out;

  Comparator #(.width(16)) comparator_1 (.a(Data1), .b(Data2), .eq(comparator_1_eq), .lt(comparator_1_lt));  // open: gt
  Adder #(.width(16)) adder_1 (.a(Data1), .b(Data2), .out(adder_1_out));  // open: cin, cout
  assign and_1_out = Data1 & Data2;  // AND_Gate and_1, 16 bits wide
  assign or_1_out = Data1 | Data2;  // OR_Gate or_1, 16 bits wide
  not bne (bne_out, comparator_1_eq);
  Multiplexer #(.select(2), .width(16)) multiplexer_1 (
    .in0(Data2), .in1(adder_1_out), .in2(and_1_out), .in3(or_1_out), .out(\output ), .sel(ALUop_2));  // open: en
  or ble (ble_out, comparator_1_eq, comparator_1_lt);
  Multiplexer multiplexer_2 (.in0(ble_out), .in1(bne_out), .out(Zero), .sel(ALUBranch));  // open: en
endmodule

module Control (
  input  [3:0] in_1,
  output reg_write,
  output ALU_source,
  output reg_dest,
  output mem_to_register,
  output ALUOp1,
  output ALUOp2,
  output clock_stop,
  output mem_read,
  output mem_write,
  output write_ra,
  output ALU_branch,
  output [1:0] branch_2
);

  regWrite regwrite_1 (.in_1(in_1), .out_2(reg_write));
  ALUSource alusource_1 (.in_1(in_1), .out_2(ALU_source));
  regDest regdest_1 (.in_1(in_1), .out_2(reg_dest));
  memToRegister memtoregister_1 (.in_1(in_1), .out_2(mem_to_register));
  ALUOp aluop_1 (.in_1(in_1), .out_2(ALUOp1), .out_3(ALUOp2));
  clockStop clockstop_1 (.in_1(in_1), .out_2(clock_stop));
  memRead memread_1 (.out_1(mem_read));
  memWrite memwrite_1 (.in_1(in_1), .out_2(mem_write));
  writeRa writera_1 (.in_1(in_1), .out_2(write_ra));
  ALUBranch alubranch_1 (.in_1(in_1), .out_2(ALU_branch));
  branch branch_1 (.in_1(in_1), .out_2(branch_2));
endmodule

module ALUSource (
  input  [3:0] in_1,
  output out_2
);

  wire and_1_out, and_2_out, and_3_out;

  and and_1 (and_1_out, ~in_1[0], ~in_1[1], ~in_1[3]);  // AND_Gate
  and and_2 (and_2_out, ~in_1[1], ~in_1[2], in_1[3]);  // AND_Gate
  and and_3 (and_3_out, in_1[0], in_1[2], ~in_1[3]);  // AND_Gate
  or or_1 (out_2, and_1_out, and_2_out, and_3_out);
endmodule

module Registers (
  input  [2:0] WriteReg,
  input  RegWrite,
  input  Clock,
  input  Reset,
  input  [15:0] WriteData,
  input  [2:0] ReadReg1,
  input  [2:0] ReadReg2,
  output [15:0] ReadData1,
  output [15:0] ReadData2
);

  wire and_1_out, and_2_out, and_3_out, and_4_out, and_5_out, and_6_out, and_7_out, and_8_out,
       decoder_1_out0, decoder_1_out1, decoder_1_out2, decoder_1_out3, decoder_1_out4, decoder_1_out5,
       decoder_1_out6, decoder_1_out7;
  wire [15:0] r1_q, r2_q, r3_q, r4_q, r5_q, r6_q, r7_q, r8_q;

  Decoder #(.select(3)) decoder_1 (
    .out0(decoder_1_out0), .out1(decoder_1_out1), .out2(decoder_1_out2), .out3(decoder_1_out3),
    .out4(decoder_1_out4), .out5(decoder_1_out5), .out6(decoder_1_out6), .out7(decoder_1_out7), .sel(WriteReg));  // open: en
  and and_1 (and_1_out, RegWrite, decoder_1_out0);
  and and_2 (and_2_out, RegWrite, decoder_1_out1);
  and and_3 (and_3_out, RegWrite, decoder_1_out2);
  and and_4 (and_4_out, RegWrite, decoder_1_out3);
  and and_5 (and_5_out, RegWrite, decoder_1_out4);
  and and_6 (and_6_out, RegWrite, decoder_1_out5);
  and and_7 (and_7_out, RegWrite, decoder_1_out6);
  and and_8 (and_8_out, RegWrite, decoder_1_out7);
  Register #(.trigger("falling"), .width(16)) r1 (.D(WriteData), .en(and_1_out), .Q(r1_q), .clk(Clock), .clr(Reset));
  Register #(.trigger("falling"), .width(16)) r2 (.D(WriteData), .en(and_2_out), .Q(r2_q), .clk(Clock), .clr(Reset));
  Register #(.trigger("falling"), .width(16)) r3 (.D(WriteData), .en(and_3_out), .Q(r3_q), .clk(Clock), .clr(Reset));
  Register #(.trigger("falling"), .width(16)) r4 (.D(WriteData), .en(and_4_out), .Q(r4_q), .clk(Clock), .clr(Reset));
  Register #(.trigger("falling"), .width(16)) r5 (.D(WriteData), .en(and_5_out), .Q(r5_q), .clk(Clock), .clr(Reset));
  Register #(.trigger("falling"), .width(16)) r6 (.D(WriteData), .en(and_6_out), .Q(r6_q), .clk(Clock), .clr(Reset));
  Register #(.trigger("falling"), .width(16)) r7 (.D(WriteData), .en(and_7_out), .Q(r7_q), .clk(Clock), .clr(Reset));
  Register #(.trigger("falling"), .width(16)) r8 (.D(WriteData), .en(and_8_out), .Q(r8_q), .clk(Clock), .clr(Reset));
  Multiplexer #(.select(3), .width(16)) multiplexer_1 (
    .in0(r1_q), .in1(r2_q), .in2(r3_q), .in3(r4_q), .in4(r5_q), .in5(r6_q), .in6(r7_q), .in7(r8_q),
    .out(ReadData1), .sel(ReadReg1));  // open: en
  Multiplexer #(.select(3), .width(16)) multiplexer_2 (
    .in0(r1_q), .in1(r2_q), .in2(r3_q), .in3(r4_q), .in4(r5_q), .in5(r6_q), .in6(r7_q), .in7(r8_q),
    .out(ReadData2), .sel(ReadReg2));  // open: en
endmodule
